// Logisim project lab7_step5.circ as structural Verilog: 1 circuit, main circuit main
module main (
  input  [15:0] in_1,
  input  [1:0] in_2,
  input  in_3,
  input  in_4,
  input  in_5,
  input  in_6,
  input  in_7,
  output [15:0] out_8
);

  wire clock_1_out, not_1_out;
  wire [15:0] controlled_buffer_1_out;

  Clock clock_1 (.out(clock_1_out));
  assign controlled_buffer_1_out = not_1_out ? in_1 : 16'bz;  // Controlled_Buffer controlled_buffer_1
  RAM #(.addrWidth(2), .dataWidth(16)) ram_1 (
    .addr(in_2), .data(controlled_buffer_1_out), .sel(in_4), .clk(clock_1_out), .ld(in_6), .clr(in_7));
  assign out_8 = in_5 ? controlled_buffer_1_out : 16'bz;  // Controlled_Buffer controlled_buffer_2
  not not_1 (not_1_out, in_5);
endmodule
