// Logisim project lab8_2.circ as structural Verilog: 1 circuit, main circuit main
module main (
  input  rst,
  input  pulse,
  output [3:0] cnt_next,
  output [3:0] cnt
);

  wire clk_out, register_1_q, xor_1_out;
  wire [3:0] adder_1_out;

  Clock clk (.out(clk_out));
  Adder #(.width(4)) adder_1 (.a(cnt), .b(4'b0001), .out(adder_1_out));  // open: cin, cout
  xor xor_1 (xor_1_out, pulse, register_1_q);
  Register #(.width(1)) register_1 (.D(pulse), .Q(register_1_q), .clk(clk_out));  // open: en, clr
  Multiplexer #(.width(4)) multiplexer_1 (.in0(cnt), .in1(adder_1_out), .out(cnt_next), .sel(xor_1_out));  // open: en
  Register #(.width(4)) register_2 (.D(cnt_next), .Q(cnt), .clk(clk_out), .clr(rst));  // open: en
endmodule
