// Logisim project week10.circ as structural Verilog: 4 circuits, main circuit main
module main (
  input  input1,
  input  input2,
  input  in_3,
  input  in_4,
  input  in_5,
  input  input3,
  input  [1:0] in_7,
  input  [1:0] in_8,
  input  [1:0] in_9,
  output output1,
  output output2,
  output output3,
  output out_13
);

  wire d_ff_1_q, decoder_1_out1, decoder_1_out2, decoder_1_out3, decoder_2_out1, decoder_2_out2,
       decoder_2_out3, decoder_3_out1, decoder_3_out2, decoder_3_out3, ram_1_data;

  Clock clock_1 ();  // open: out
  RAM #(.addrWidth(2), .dataWidth(1)) ram_1 (.addr({in_4, in_5}), .data(ram_1_data));  // open: sel, clk, ld, clr
  D_Flip_Flop d_ff_1 (.clk(in_3), .D(ram_1_data), .Q(d_ff_1_q));  // open: Qn, preset, en, reset
  Multiplexer multiplexer_1 (.in0(d_ff_1_q), .in1(ram_1_data), .out(out_13), .sel(1'b1));  // open: en
  Decoder #(.select(2)) decoder_1 (
    .out1(decoder_1_out1), .out2(decoder_1_out2), .out3(decoder_1_out3), .sel(in_7));  // open: out0, en
  assign output1 = decoder_1_out1 ? input1 : 1'bz;  // Controlled_Buffer controlled_buffer_1
  assign output1 = decoder_1_out2 ? input2 : 1'bz;  // Controlled_Buffer controlled_buffer_2
  assign output1 = decoder_1_out3 ? input3 : 1'bz;  // Controlled_Buffer controlled_buffer_3
  Decoder #(.select(2)) decoder_2 (
    .out1(decoder_2_out1), .out2(decoder_2_out2), .out3(decoder_2_out3), .sel(in_8));  // open: out0, en
  assign output2 = decoder_2_out1 ? input1 : 1'bz;  // Controlled_Buffer controlled_buffer_4
  assign output2 = decoder_2_out2 ? input2 : 1'bz;  // Controlled_Buffer controlled_buffer_5
  assign output2 = decoder_2_out3 ? input3 : 1'bz;  // Controlled_Buffer controlled_buffer_6
  assign output3 = decoder_3_out1 ? input1 : 1'bz;  // Controlled_Buffer controlled_buffer_7
  assign output3 = decoder_3_out2 ? input2 : 1'bz;  // Controlled_Buffer controlled_buffer_8
  assign output3 = decoder_3_out3 ? input3 : 1'bz;  // Controlled_Buffer controlled_buffer_9
  Decoder #(.select(2)) decoder_3 (
    .out1(decoder_3_out1), .out2(decoder_3_out2), .out3(decoder_3_out3), .sel(in_9));  // open: out0, en
endmodule

module lab6_step4 (
  input  input1,
  input  input2,
  input  input3,
  input  [1:0] in_4,
  input  [1:0] in_5,
  input  [1:0] in_6,
  output output1,
  output output2,
  output output3
);

  wire decoder_1_out1, decoder_1_out2, decoder_1_out3, decoder_2_out1, decoder_2_out2, decoder_2_out3,
       decoder_3_out1, decoder_3_out2, decoder_3_out3;

  assign output1 = decoder_1_out1 ? input1 : 1'bz;  // Controlled_Buffer controlled_buffer_1
  assign output1 = decoder_1_out2 ? input2 : 1'bz;  // Controlled_Buffer controlled_buffer_2
  assign output1 = decoder_1_out3 ? input3 : 1'bz;  // Controlled_Buffer controlled_buffer_3
  Decoder #(.select(2)) decoder_1 (
    .out1(decoder_1_out1), .out2(decoder_1_out2), .out3(decoder_1_out3), .sel(in_4));  // open: out0, en
  assign output2 = decoder_2_out1 ? input1 : 1'bz;  // Controlled_Buffer controlled_buffer_4
  assign output2 = decoder_2_out2 ? input2 : 1'bz;  // Controlled_Buffer controlled_buffer_5
  assign output2 = decoder_2_out3 ? input3 : 1'bz;  // Controlled_Buffer controlled_buffer_6
  Decoder #(.select(2)) decoder_2 (
    .out1(decoder_2_out1), .out2(decoder_2_out2), .out3(decoder_2_out3), .sel(in_5));  // open: out0, en
  Decoder #(.select(2)) decoder_3 (
    .out1(decoder_3_out1), .out2(decoder_3_out2), .out3(decoder_3_out3), .sel(in_6));  // open: out0, en
  assign output3 = decoder_3_out1 ? input1 : 1'bz;  // Controlled_Buffer controlled_buffer_7
  assign output3 = decoder_3_out2 ? input2 : 1'bz;  // Controlled_Buffer controlled_buffer_8
  assign output3 = decoder_3_out3 ? input3 : 1'bz;  // Controlled_Buffer controlled_buffer_9
endmodule

module lab6_step4_2 (
  input  input1,
  input  input2,
  input  clk,
  input  a,
  input  b,
  output output1,
  output output2,
  output output3
);

  wire d_ff_1_q, decoder_1_out1, decoder_1_out2, decoder_1_out3, decoder_2_out1, decoder_2_out2,
       decoder_2_out3, decoder_3_out1, decoder_3_out2, decoder_3_out3, multiplexer_2_out, ram_1_data;
  wire [0:0] multiplexer_1_out;

  Multiplexer multiplexer_1 (.in0(output1), .in1(a), .out(multiplexer_1_out[0]), .sel(1'b1));  // open: en
  RAM #(.addrWidth(2), .dataWidth(1)) ram_1 (
    .addr({b, multiplexer_1_out[0]}), .data(ram_1_data));  // open: sel, clk, ld, clr
  D_Flip_Flop d_ff_1 (.clk(clk), .D(ram_1_data), .Q(d_ff_1_q));  // open: Qn, preset, en, reset
  Multiplexer multiplexer_2 (.in0(d_ff_1_q), .in1(ram_1_data), .out(multiplexer_2_out), .sel(1'b1));  // open: en
  Decoder #(.select(2)) decoder_1 (
    .out1(decoder_1_out1), .out2(decoder_1_out2), .out3(decoder_1_out3), .sel(2'b11));  // open: out0, en
  assign output1 = decoder_1_out1 ? input1 : 1'bz;  // Controlled_Buffer controlled_buffer_1
  assign output1 = decoder_1_out2 ? input2 : 1'bz;  // Controlled_Buffer controlled_buffer_2
  assign output1 = decoder_1_out3 ? multiplexer_2_out : 1'bz;  // Controlled_Buffer controlled_buffer_3
  Decoder #(.select(2)) decoder_2 (
    .out1(decoder_2_out1), .out2(decoder_2_out2), .out3(decoder_2_out3), .sel(2'b01));  // open: out0, en
  assign output2 = decoder_2_out1 ? input1 : 1'bz;  // Controlled_Buffer controlled_buffer_4
  assign output2 = decoder_2_out2 ? input2 : 1'bz;  // Controlled_Buffer controlled_buffer_5
  assign output2 = decoder_2_out3 ? multiplexer_2_out : 1'bz;  // Controlled_Buffer controlled_buffer_6
  Decoder #(.select(2)) decoder_3 (
    .out1(decoder_3_out1), .out2(decoder_3_out2), .out3(decoder_3_out3), .sel(2'b10));  // open: out0, en
  assign output3 = decoder_3_out1 ? input1 : 1'bz;  // Controlled_Buffer controlled_buffer_7
  assign output3 = decoder_3_out2 ? input2 : 1'bz;  // Controlled_Buffer controlled_buffer_8
  assign output3 = decoder_3_out3 ? multiplexer_2_out : 1'bz;  // Controlled_Buffer controlled_buffer_9
endmodule

module lab6_step4_3 (
  input  input1,
  input  clk,
  input  input2,
  input  a,
  input  b,
  output output1,
  output output2,
  output output3,
  output \引脚A ,
  output \引脚B 
);

  wire buffer_1_out, buffer_2_out, clock_1_out, d_ff_1_q, decoder_1_out1, decoder_1_out2, decoder_1_out3,
       decoder_2_out1, decoder_2_out2, decoder_2_out3, decoder_3_out1, decoder_3_out2, decoder_3_out3,
       multiplexer_2_out, ram_1_data;
  wire [0:0] multiplexer_1_out;

  Clock clock_1 (.out(clock_1_out));
  Multiplexer multiplexer_1 (.in0(output1), .in1(a), .out(multiplexer_1_out[0]), .sel(1'b0));  // open: en
  RAM #(.addrWidth(2), .dataWidth(1)) ram_1 (
    .addr({b, multiplexer_1_out[0]}), .data(ram_1_data));  // open: sel, clk, ld, clr
  D_Flip_Flop d_ff_1 (.clk(clock_1_out), .D(ram_1_data), .Q(d_ff_1_q));  // open: Qn, preset, en, reset
  Multiplexer multiplexer_2 (.in0(d_ff_1_q), .in1(ram_1_data), .out(multiplexer_2_out), .sel(1'b0));  // open: en
  Decoder #(.select(2)) decoder_1 (
    .out1(decoder_1_out1), .out2(decoder_1_out2), .out3(decoder_1_out3), .sel(2'b11));  // open: out0, en
  assign output1 = decoder_1_out1 ? input1 : 1'bz;  // Controlled_Buffer controlled_buffer_1
  assign output1 = decoder_1_out2 ? input2 : 1'bz;  // Controlled_Buffer controlled_buffer_2
  assign output1 = decoder_1_out3 ? multiplexer_2_out : 1'bz;  // Controlled_Buffer controlled_buffer_3
  Decoder #(.select(2)) decoder_2 (
    .out1(decoder_2_out1), .out2(decoder_2_out2), .out3(decoder_2_out3), .sel(2'b01));  // open: out0, en
  assign output2 = decoder_2_out1 ? input1 : 1'bz;  // Controlled_Buffer controlled_buffer_4
  assign output2 = decoder_2_out2 ? input2 : 1'bz;  // Controlled_Buffer controlled_buffer_5
  assign output2 = decoder_2_out3 ? multiplexer_2_out : 1'bz;  // Controlled_Buffer controlled_buffer_6
  Decoder #(.select(2)) decoder_3 (
    .out1(decoder_3_out1), .out2(decoder_3_out2), .out3(decoder_3_out3), .sel(2'b11));  // open: out0, en
  assign output3 = decoder_3_out1 ? input1 : 1'bz;  // Controlled_Buffer controlled_buffer_7
  assign output3 = decoder_3_out2 ? input2 : 1'bz;  // Controlled_Buffer controlled_buffer_8
  assign output3 = decoder_3_out3 ? multiplexer_2_out : 1'bz;  // Controlled_Buffer controlled_buffer_9
  buf buffer_1 (buffer_1_out, \引脚A );
  buf buffer_2 (buffer_2_out, \引脚B );
  assign \引脚A  = 1'b1 ? output2 : 1'bz;  // Controlled_Buffer controlled_buffer_10
  assign \引脚B  = 1'b1 ? output3 : 1'bz;  // Controlled_Buffer controlled_buffer_11
endmodule
