// Logisim project week5.circ as structural Verilog
module exercise1 (
);

  DotMatrix #(.inputtype("row"), .matrixcols(16), .matrixrows(16)) dotmatrix_1 (
    .row0(16'h200), .row1(16'h100), .row2(16'hfffe), .row3({16{1'b0}}), .row4(16'hfe0), .row5(16'h820),
    .row6(16'h820), .row7(16'hfe0), .row8({16{1'b0}}), .row9(16'h7ffc), .row10(16'h4004), .row11(16'h4fe4),
    .row12(16'h4824), .row13(16'h4824), .row14(16'h4fe4), .row15(16'h400c));
  DotMatrix #(.inputtype("row"), .matrixcols(16), .matrixrows(16)) dotmatrix_2 (
    .row0(16'h820), .row1(16'h820), .row2(16'h7efc), .row3(16'h820), .row4(16'h1c70), .row5(16'h2aa8),
    .row6(16'hc824), .row7({16{1'b0}}), .row8(16'h7ffc), .row9(16'h104), .row10(16'h1100), .row11(16'h11f8),
    .row12(16'h1100), .row13(16'h2900), .row14(16'h47fe), .row15(16'h8000));
  DotMatrix #(.inputtype("row"), .matrixcols(16), .matrixrows(16)) dotmatrix_3 (
    .row0(16'h20), .row1(16'h20), .row2(16'h7bfe), .row3(16'h4820), .row4(16'h49fc), .row5(16'h4820),
    .row6(16'h4bfe), .row7(16'h7800), .row8(16'h49fc), .row9(16'h4904), .row10(16'h49fc), .row11(16'h4904),
    .row12(16'h79fc), .row13(16'h4904), .row14(16'h114), .row15(16'h108));
endmodule

module exercise2 (
  input  in_1,
  input  in_2,
  input  in_3,
  input  in_4,
  input  in_5,
  input  in_6,
  input  in_7,
  input  in_8,
  input  in_9,
  input  in_10,
  input  in_11,
  input  in_12,
  input  in_13,
  input  in_14,
  input  in_15,
  input  in_16,
  input  in_17,
  input  in_18,
  input  in_19,
  input  in_20,
  input  in_21,
  input  in_22,
  input  in_23,
  input  in_24,
  input  in_25,
  input  in_26,
  input  in_27,
  input  in_28,
  input  in_29,
  input  in_30,
  input  in_31,
  input  in_32,
  input  in_33,
  input  in_34,
  input  in_35,
  input  in_36,
  input  in_37,
  input  in_38,
  input  in_39,
  input  in_40,
  input  in_41,
  input  in_42,
  input  in_43,
  input  in_44,
  input  in_45,
  input  in_46,
  input  in_47,
  input  in_48,
  input  in_49,
  input  in_50,
  input  in_51,
  input  in_52,
  input  in_53,
  input  in_54,
  input  in_55,
  input  in_56,
  input  in_57,
  input  in_58,
  input  in_59,
  input  in_60,
  input  in_61,
  input  in_62,
  input  in_63,
  input  in_64,
  input  in_65,
  input  in_66,
  input  in_67,
  input  in_68,
  input  in_69,
  input  in_70,
  input  in_71,
  input  in_72,
  input  in_73,
  input  in_74,
  input  in_75,
  input  in_76,
  input  in_77,
  input  in_78,
  input  in_79,
  input  in_80
);

  _7_Segment_Display u_7_segment_display_1 (
    .g(in_21), .f(in_1), .a(in_2), .b(in_22), .e(in_41), .d(in_61), .c(in_62), .dp(in_42));
  _7_Segment_Display u_7_segment_display_2 (
    .g(in_23), .f(in_3), .a(in_4), .b(in_24), .e(in_43), .d(in_63), .c(in_64), .dp(in_44));
  _7_Segment_Display u_7_segment_display_3 (
    .g(in_25), .f(in_5), .a(in_6), .b(in_26), .e(in_45), .d(in_65), .c(in_66), .dp(in_46));
  _7_Segment_Display u_7_segment_display_4 (
    .g(in_27), .f(in_7), .a(in_8), .b(in_28), .e(in_47), .d(in_67), .c(in_68), .dp(in_48));
  _7_Segment_Display u_7_segment_display_5 (
    .g(in_29), .f(in_9), .a(in_10), .b(in_30), .e(in_49), .d(in_69), .c(in_70), .dp(in_50));
  _7_Segment_Display u_7_segment_display_6 (
    .g(in_31), .f(in_11), .a(in_12), .b(in_32), .e(in_51), .d(in_71), .c(in_72), .dp(in_52));
  _7_Segment_Display u_7_segment_display_7 (
    .g(in_33), .f(in_13), .a(in_14), .b(in_34), .e(in_53), .d(in_73), .c(in_74), .dp(in_54));
  _7_Segment_Display u_7_segment_display_8 (
    .g(in_35), .f(in_15), .a(in_16), .b(in_36), .e(in_55), .d(in_75), .c(in_76), .dp(in_56));
  _7_Segment_Display u_7_segment_display_9 (
    .g(in_37), .f(in_17), .a(in_18), .b(in_38), .e(in_57), .d(in_77), .c(in_78), .dp(in_58));
  _7_Segment_Display u_7_segment_display_10 (
    .g(in_39), .f(in_19), .a(in_20), .b(in_40), .e(in_59), .d(in_79), .c(in_80), .dp(in_60));
endmodule

module exercise3_1_and (
  input  in_1,
  input  in_2,
  output out_3
);

  wire transistor_2_out;

  Transistor transistor_1 (.in(1'b0), .out(out_3), .gate(in_2));
  Transistor #(.\type ("n")) transistor_2 (.in(1'b1), .out(transistor_2_out), .gate(in_1));
  Transistor #(.\type ("n")) transistor_3 (.in(transistor_2_out), .out(out_3), .gate(in_2));
  Transistor transistor_4 (.in(1'b0), .out(out_3), .gate(in_1));

  // Notes on the sheet:
  //                       高楚晴_PB18111688
  //   与门
endmodule

module exercise3_2_or (
  input  in_1,
  input  in_2,
  output out_3
);

  wire transistor_3_out;

  Transistor #(.\type ("n")) transistor_1 (.in(1'b1), .out(out_3), .gate(in_1));
  Transistor transistor_2 (.in(transistor_3_out), .out(out_3), .gate(in_2));
  Transistor transistor_3 (.in(1'b0), .out(transistor_3_out), .gate(in_1));
  Transistor #(.\type ("n")) transistor_4 (.in(1'b1), .out(out_3), .gate(in_2));

  // Notes on the sheet:
  //   或门
  //   高楚晴_PB18111688
endmodule

module exercise3_3_not (
  input  in_1,
  output out_2
);

  Transistor transistor_1 (.in(1'b1), .out(out_2), .gate(in_1));
  Transistor #(.\type ("n")) transistor_2 (.in(1'b0), .out(out_2), .gate(in_1));

  // Notes on the sheet:
  //                         非门
  //   高楚晴_PB18111688
endmodule

module exercise3_4_nor (
  input  in_1,
  input  in_2,
  output out_3
);

  wire transistor_2_out;

  Transistor #(.\type ("n")) transistor_1 (.in(1'b0), .out(out_3), .gate(in_2));
  Transistor transistor_2 (.in(1'b1), .out(transistor_2_out), .gate(in_1));
  Transistor transistor_3 (.in(transistor_2_out), .out(out_3), .gate(in_2));
  Transistor #(.\type ("n")) transistor_4 (.in(1'b0), .out(out_3), .gate(in_1));

  // Notes on the sheet:
  //                             或非门
  //   高楚晴_PB18111688
endmodule

module exercise3_5_nand (
  input  in_1,
  input  in_2,
  output out_3
);

  wire transistor_3_out;

  Transistor transistor_1 (.in(1'b1), .out(out_3), .gate(in_1));
  Transistor #(.\type ("n")) transistor_2 (.in(transistor_3_out), .out(out_3), .gate(in_1));
  Transistor #(.\type ("n")) transistor_3 (.in(1'b0), .out(transistor_3_out), .gate(in_2));
  Transistor transistor_4 (.in(1'b1), .out(out_3), .gate(in_2));

  // Notes on the sheet:
  //                 与非门
  //   高楚晴_PB18111688
endmodule

module exercise4 (
  input  S,
  input  A,
  input  B,
  output L
);

  wire exercise3_1_and_1_out_3, exercise3_1_and_2_out_3, exercise3_3_not_1_out_2;

  exercise3_3_not exercise3_3_not_1 (.in_1(S), .out_2(exercise3_3_not_1_out_2));
  exercise3_1_and exercise3_1_and_1 (.in_1(S), .in_2(A), .out_3(exercise3_1_and_1_out_3));
  exercise3_1_and exercise3_1_and_2 (.in_1(exercise3_3_not_1_out_2), .in_2(B), .out_3(exercise3_1_and_2_out_3));
  exercise3_2_or exercise3_2_or_1 (.in_1(exercise3_1_and_1_out_3), .in_2(exercise3_1_and_2_out_3), .out_3(L));

  // Notes on the sheet:
  //   若以基本门搭建数据选择器
  //   2选1需要2个与门，1个或门，1个非门
  //   4选1需要4个与门，1个或门，4个非门
  //   说明：
  //   S为控制端，当S值为0时输出B的值
  //   当S值为1时输出A的值
endmodule

module exercise4_2 (
  input  S2_1,
  input  S2_0,
  input  S1_1,
  input  S1_0,
  input  D2,
  input  B2,
  input  C2,
  input  A2,
  input  D1,
  input  B1,
  input  C1,
  input  A1,
  output L2,
  output L1
);

  wire exercise4_1_l, exercise4_2_l, exercise4_3_l, exercise4_4_l;

  exercise4 exercise4_1 (.A(D2), .B(B2), .L(exercise4_1_l), .S(S2_1));
  exercise4 exercise4_2 (.A(C2), .B(A2), .L(exercise4_2_l), .S(S2_1));
  exercise4 exercise4_3 (.A(D1), .B(B1), .L(exercise4_3_l), .S(S1_1));
  exercise4 exercise4_4 (.A(C1), .B(A1), .L(exercise4_4_l), .S(S1_1));
  exercise4 exercise4_5 (.A(exercise4_1_l), .B(exercise4_2_l), .L(L2), .S(S2_0));
  exercise4 exercise4_6 (.A(exercise4_3_l), .B(exercise4_4_l), .L(L1), .S(S1_0));

  // Notes on the sheet:
  //   对i = 1,2
  //   Si=00,输出Ai
  //   Si=01,输出Bi
  //   Si = 10,输出Ci
  //   Si = 11,输出Di
endmodule
