// Logisim project week5plus.circ as structural Verilog: 1 circuit, main circuit main
module main (
  input  \输入管脚 ,
  input  [7:0] \分线器 ,
  output \输出管脚 
);

  wire button_1_out;

  Button button_1 (.out(button_1_out));
  // Probe on \分线器 [3:0]
  // Probe on \分线器 [7:4]
  LED led_1 (.in(button_1_out));
  // Probe on \分线器 [3:0]
  // Probe on \分线器 [7:4]
  // Probe on \分线器 [3:0]
  // Probe on \分线器 [7:4]
  // Probe on \分线器 [1:0]
  // Probe on \分线器 [3:2]
  // Probe on \分线器 [5:4]
  // Probe on \分线器 [7:6]

  assign \输出管脚  = \输入管脚 ;

  // Notes on the sheet:
  //   按钮
  //   LED
endmodule
