// Logisim project week6.circ as structural Verilog: 5 circuits, main circuit exercise1
module exercise1 (
  input  Ci1,
  input  Ai,
  input  Bi,
  output Si,
  output Ci
);

  wire and_1_out, and_2_out, and_3_out, and_4_out, and_5_out, and_6_out, and_7_out, not_1_out, not_2_out,
       not_3_out, not_4_out, not_5_out, not_6_out;

  not not_1 (not_1_out, Ci1);
  not not_2 (not_2_out, Ai);
  not not_3 (not_3_out, Ci1);
  not not_4 (not_4_out, Bi);
  not not_5 (not_5_out, Ai);
  not not_6 (not_6_out, Bi);
  and and_1 (and_1_out, Ai, Bi);
  and and_2 (and_2_out, Ci1, Bi);
  and and_3 (and_3_out, Ci1, Ai);
  and and_4 (and_4_out, not_1_out, not_2_out, Bi);
  and and_5 (and_5_out, not_3_out, Ai, not_4_out);
  and and_6 (and_6_out, Ci1, not_5_out, not_6_out);
  and and_7 (and_7_out, Ci1, Ai, Bi);
  or or_1 (Ci, and_1_out, and_2_out, and_3_out);
  or or_2 (Si, and_4_out, and_5_out, and_6_out, and_7_out);

  // Notes on the sheet:
  //   PB18111688 高楚晴
endmodule

module exercise2 (
  input  G1,
  input  G2,
  input  G3,
  input  A2,
  input  A1,
  input  A0,
  output Y7,
  output Y6,
  output Y5,
  output Y4,
  output Y3,
  output Y2,
  output Y1,
  output Y0
);

  wire not_1_out, not_2_out, not_3_out, not_4_out, not_5_out, not_6_out, not_7_out, not_8_out, not_9_out,
       not_10_out, not_11_out, not_12_out, not_13_out, not_14_out, not_15_out, not_16_out, not_17_out,
       not_18_out, not_19_out, not_20_out, not_21_out;

  not not_1 (not_1_out, G1);
  not not_2 (not_2_out, A2);
  not not_3 (not_3_out, A1);
  not not_4 (not_4_out, A0);
  not not_5 (not_5_out, G1);
  not not_6 (not_6_out, A2);
  not not_7 (not_7_out, A1);
  not not_8 (not_8_out, G1);
  not not_9 (not_9_out, A2);
  not not_10 (not_10_out, A0);
  not not_11 (not_11_out, G1);
  not not_12 (not_12_out, A2);
  not not_13 (not_13_out, A1);
  not not_14 (not_14_out, G1);
  not not_15 (not_15_out, A1);
  not not_16 (not_16_out, A0);
  not not_17 (not_17_out, G1);
  not not_18 (not_18_out, A1);
  not not_19 (not_19_out, G1);
  not not_20 (not_20_out, A0);
  not not_21 (not_21_out, G1);
  or or_1 (Y7, not_1_out, G2, G3, not_2_out, not_3_out, not_4_out);
  or or_2 (Y6, not_5_out, G2, G3, not_6_out, not_7_out, A0);
  or or_3 (Y5, not_8_out, G2, G3, not_9_out, A1, not_10_out);
  or or_4 (Y4, not_11_out, G2, G3, not_12_out, not_13_out, A0);
  or or_5 (Y3, not_14_out, G2, G3, A2, not_15_out, not_16_out);
  or or_6 (Y2, not_17_out, G2, G3, A2, not_18_out, A0);
  or or_7 (Y1, not_19_out, G2, G3, A2, A1, not_20_out);
  or or_8 (Y0, not_21_out, G2, G3, A2, A1, A0);

  // Notes on the sheet:
  //   PB18111688 高楚晴
endmodule

module exercise3 (
  input  sel,
  input  b,
  input  a,
  output out
);

  wire and_1_out, and_2_out, not_1_out;

  not not_1 (not_1_out, sel);
  and and_1 (and_1_out, sel, b);
  and and_2 (and_2_out, not_1_out, a);
  or or_1 (out, and_1_out, and_2_out);

  // Notes on the sheet:
  //   PB18111688 高楚晴 
endmodule

module exercise4 (
  input  sel1,
  input  sel0,
  input  d,
  input  c,
  input  b,
  input  a,
  output out
);

  wire exercise3_1_out, exercise3_2_out;

  exercise3 exercise3_1 (.b(d), .a(b), .out(exercise3_1_out), .sel(sel1));
  exercise3 exercise3_2 (.b(c), .a(a), .out(exercise3_2_out), .sel(sel1));
  exercise3 exercise3_3 (.b(exercise3_1_out), .a(exercise3_2_out), .out(out), .sel(sel0));

  // Notes on the sheet:
  //   PB18111688 高楚晴
  //   w2
  //   w1
endmodule

module exercise6 (
  input  a,
  input  b,
  input  c,
  output s1,
  output s2
);

  wire and_1_out, and_2_out, and_3_out, and_4_out, and_5_out, and_6_out, and_7_out, and_8_out, not_1_out,
       not_2_out, not_3_out, not_4_out, not_5_out, not_6_out, not_7_out, not_8_out, not_9_out, not_10_out,
       not_11_out, not_12_out;

  not not_1 (not_1_out, a);
  not not_2 (not_2_out, b);
  not not_3 (not_3_out, a);
  not not_4 (not_4_out, c);
  not not_5 (not_5_out, b);
  not not_6 (not_6_out, c);
  not not_7 (not_7_out, a);
  not not_8 (not_8_out, b);
  not not_9 (not_9_out, c);
  not not_10 (not_10_out, a);
  not not_11 (not_11_out, b);
  not not_12 (not_12_out, c);
  and and_1 (and_1_out, not_1_out, not_2_out, c);
  and and_2 (and_2_out, not_3_out, b, not_4_out);
  and and_3 (and_3_out, a, not_5_out, not_6_out);
  and and_4 (and_4_out, a, b, c);
  and and_5 (and_5_out, not_7_out, not_8_out, not_9_out);
  and and_6 (and_6_out, not_10_out, b, c);
  and and_7 (and_7_out, a, not_11_out, c);
  and and_8 (and_8_out, a, b, not_12_out);
  or or_1 (s1, and_1_out, and_2_out, and_3_out, and_4_out);
  or or_2 (s2, and_5_out, and_6_out, and_7_out, and_8_out);

  // Notes on the sheet:
  //   电路功能：
  //   有奇数个1时s1为1
  //   有奇数个0时s2为1
endmodule
