// Logisim project 实验3.circ as structural Verilog
module main (
  input  in_1,
  input  in_2,
  output out_3,
  output out_4,
  output out_5,
  output out_6
);

  not not_1 (out_4, out_6);
  not not_2 (out_6, out_4);
  not not_3 (out_3, out_5);
  not not_4 (out_5, out_3);

  // Notes on the sheet:
  //   PB18111733 蒲明昱
endmodule

module D (
  input  CLK,
  input  D,
  output Q,
  output nQ
);

  wire and_1_out, and_2_out, not_1_out;

  not not_1 (not_1_out, D);
  and and_1 (and_1_out, CLK, not_1_out);
  and and_2 (and_2_out, CLK, D);
  SR sr_1 (.R(and_1_out), .S(and_2_out), .Q(Q), .nQ(nQ));
endmodule

module SR (
  input  R,
  input  S,
  output Q,
  output nQ
);

  nor nor_1 (Q, R, nQ);
  nor nor_2 (nQ, Q, S);

  // Notes on the sheet:
  //   PB18111733 蒲明昱
endmodule

module \D触发器  (
  input  CLK,
  input  D,
  output out_3,
  output out_4
);

  wire d_1_q, not_1_out;

  not not_1 (not_1_out, CLK);
  D d_1 (.CLK(not_1_out), .D(D), .Q(d_1_q));  // open: nQ
  D d_2 (.CLK(CLK), .D(d_1_q), .Q(out_3), .nQ(out_4));
endmodule

module \同步复位D触发器  (
  input  CLK,
  input  D,
  input  nRST,
  output Q,
  output nQ
);

  wire and_1_out;

  and and_1 (and_1_out, D, nRST);
  \D触发器  \d触发器_1  (.D(CLK), .out_3(Q), .out_4(nQ), .CLK(and_1_out));

  // Notes on the sheet:
  //   同步复位
endmodule

module \计数器  (
  input  in_1,
  output [3:0] out_2
);

  wire clock_1_out;
  wire [3:0] adder_1_out;

  Clock clock_1 (.out(clock_1_out));
  Adder #(.width(4)) adder_1 (.a(out_2), .b(4'b0001), .out(adder_1_out), .cin(1'b0));  // open: cout
  \例_寄存器  \u_例_寄存器_1  (.in_1(adder_1_out), .in_2(clock_1_out), .RST_N(in_1), .out_4(out_2));
  \寄存器  \u_寄存器_1  ();
  \寄存器  \u_寄存器_2  ();
endmodule

module _1 (
  input  nS,
  input  nR,
  output Q,
  output nQ
);

  nand nand_1 (Q, nS, nQ);
  nand nand_2 (nQ, Q, nR);

  // Notes on the sheet:
  //   PB18111733 蒲明昱
endmodule

module _2 (
  input  D,
  input  SET,
  output out_3,
  output out_4
);

  wire clock_1_out, or_1_out;

  Clock clock_1 (.out(clock_1_out));
  or or_1 (or_1_out, D, SET);
  \D触发器  \d触发器_1  (.D(clock_1_out), .out_3(out_3), .out_4(out_4), .CLK(or_1_out));

  // Notes on the sheet:
  //   同步置位
endmodule

module \例_寄存器  (
  input  [3:0] in_1,
  input  in_2,
  input  RST_N,
  output [3:0] out_4
);

  wire and_1_out, and_2_out, and_3_out, and_4_out;

  and and_1 (and_1_out, RST_N, in_1[0]);
  and and_2 (and_2_out, RST_N, in_1[1]);
  and and_3 (and_3_out, RST_N, in_1[2]);
  and and_4 (and_4_out, RST_N, in_1[3]);
  \D触发器  \d触发器_1  (.D(in_2), .out_3(out_4[0]), .CLK(and_1_out));  // open: out_4
  \D触发器  \d触发器_2  (.D(in_2), .out_3(out_4[1]), .CLK(and_2_out));  // open: out_4
  \D触发器  \d触发器_3  (.D(in_2), .out_3(out_4[2]), .CLK(and_3_out));  // open: out_4
  \D触发器  \d触发器_4  (.D(in_2), .out_3(out_4[3]), .CLK(and_4_out));  // open: out_4
endmodule

module _3_1 (
  input  in_1,
  input  in_2,
  input  in_3,
  output out_4
);

  wire and_1_out, d_1_q, or_1_out, or_2_out;

  or or_1 (or_1_out, ~in_1, ~in_3);  // OR_Gate
  and and_1 (and_1_out, in_2, in_3);
  or or_2 (or_2_out, ~in_3, in_1);  // OR_Gate
  D d_1 (.CLK(or_1_out), .D(and_1_out), .Q(d_1_q));  // open: nQ
  D d_2 (.CLK(or_2_out), .D(d_1_q), .Q(out_4));  // open: nQ

  // Notes on the sheet:
  //   PB18111733 蒲明昱
endmodule

module \_3_2_寄存器  (
  input  [3:0] D,
  input  CLK,
  input  RST_N,
  output [3:0] out_4
);

  _3_1 u_3_1_1 (.in_1(CLK), .in_2(D[0]), .in_3(RST_N), .out_4(out_4[0]));
  _3_1 u_3_1_2 (.in_1(CLK), .in_2(D[1]), .in_3(RST_N), .out_4(out_4[1]));
  _3_1 u_3_1_3 (.in_1(CLK), .in_2(D[2]), .in_3(RST_N), .out_4(out_4[2]));
  _3_1 u_3_1_4 (.in_1(CLK), .in_2(D[3]), .in_3(RST_N), .out_4(out_4[3]));
endmodule

module \_3_3加法器  (
  input  RSET,
  output [3:0] out_2
);

  wire clock_1_out;
  wire [3:0] adder_1_out;

  Clock clock_1 (.out(clock_1_out));
  Adder #(.width(4)) adder_1 (.a(out_2), .b(4'b0001), .out(adder_1_out), .cin(1'b0));  // open: cout
  \寄存器  \u_寄存器_1  ();
  \_3_2_寄存器  \u_3_2_寄存器_1  (.D(adder_1_out), .CLK(clock_1_out), .RST_N(RSET), .out_4(out_2));

  // Notes on the sheet:
  //   CLK
  //   寄存器
endmodule

module _4 (
  input  in_1,
  output [3:0] out_2
);

  wire and_1_out, clock_1_out, or_1_out;
  wire [3:0] subtractor_1_out;

  Clock clock_1 (.out(clock_1_out));
  Subtractor #(.width(4)) subtractor_1 (.a(out_2), .b(4'b0001), .out(subtractor_1_out), .bin(1'b0));  // open: bout
  and and_1 (and_1_out, in_1, or_1_out);
  or or_1 (or_1_out, out_2[0], out_2[1], out_2[2], out_2[3]);
  \_4寄存器封装  \u_4寄存器封装_1  (.in_1(subtractor_1_out), .out_4(out_2), .CLK(clock_1_out), .RSET(and_1_out));
endmodule

module \同步置位_clock  (
  input  in_1,
  input  D,
  input  SET,
  output out_4,
  output out_5
);

  wire or_1_out;

  or or_1 (or_1_out, D, SET);
  \D触发器  \d触发器_1  (.D(in_1), .out_3(out_4), .out_4(out_5), .CLK(or_1_out));
endmodule

module \_4寄存器封装  (
  input  [3:0] in_1,
  input  RSET,
  input  CLK,
  output [3:0] out_4
);

  wire and_1_out, and_2_out, not_1_out, not_2_out, or_1_out, or_2_out;

  not not_1 (not_1_out, RSET);
  not not_2 (not_2_out, RSET);
  or or_1 (or_1_out, in_1[0], not_1_out);
  and and_1 (and_1_out, RSET, in_1[1]);
  and and_2 (and_2_out, in_1[2], RSET);
  or or_2 (or_2_out, in_1[3], not_2_out);
  \D触发器  \d触发器_1  (.D(CLK), .out_3(out_4[0]), .CLK(or_1_out));  // open: out_4
  \D触发器  \d触发器_2  (.D(CLK), .out_3(out_4[1]), .CLK(and_1_out));  // open: out_4
  \D触发器  \d触发器_3  (.D(CLK), .out_3(out_4[2]), .CLK(and_2_out));  // open: out_4
  \D触发器  \d触发器_4  (.D(CLK), .out_3(out_4[3]), .CLK(or_2_out));  // open: out_4
endmodule

module _5 (
  input  in_1,
  input  in_2,
  output out_3,
  output out_4
);

  wire clock_1_out, not_1_out;

  Clock clock_1 (.out(clock_1_out));
  not not_1 (not_1_out, in_2);
  \同步复位D触发器  \u_同步复位d触发器_1  (.CLK(clock_1_out), .D(in_1), .nRST(not_1_out), .Q(out_3), .nQ(out_4));
endmodule
