// Logisim project week7-124.circ as structural Verilog: 12 circuits, main circuit main
module main (
  output out_1,
  output out_2
);

  not not_1 (out_1, out_2);
  not not_2 (out_2, out_1);
endmodule

module SRlatch (
  input  R,
  input  S,
  output Q,
  output nQ
);

  nor nor_1 (Q, R, nQ);
  nor nor_2 (nQ, Q, S);
endmodule

module dlatch (
  input  CLK,
  input  D,
  output Q,
  output out_4
);

  wire and_1_out, and_2_out, not_1_out;

  Clock clock_1 ();  // open: out
  not not_1 (not_1_out, D);
  and and_1 (and_1_out, CLK, not_1_out);
  and and_2 (and_2_out, CLK, D);
  SRlatch srlatch_1 (.R(and_1_out), .S(and_2_out), .Q(Q), .nQ(out_4));
endmodule

module dff (
  input  CLK,
  input  D,
  output Q,
  output nQ
);

  wire dlatch_1_q, not_1_out;

  Clock clock_1 ();  // open: out
  not not_1 (not_1_out, CLK);
  dlatch dlatch_1 (.CLK(not_1_out), .D(D), .Q(dlatch_1_q));  // open: out_4
  dlatch dlatch_2 (.CLK(CLK), .D(dlatch_1_q), .Q(Q), .out_4(nQ));
endmodule

module _5 (
  input  D,
  input  nRST,
  output Q,
  output nQ
);

  wire and_1_out, CLK_out;

  Clock CLK (.out(CLK_out));
  and and_1 (and_1_out, D, nRST);
  dff dff_1 (.CLK(CLK_out), .D(and_1_out), .Q(Q), .nQ(nQ));
endmodule

module _6 (
  input  [3:0] D_IN,
  input  in_2,
  input  RST_N,
  output [3:0] D_OUT
);

  wire and_1_out, and_2_out, and_3_out, and_4_out;

  Clock CLK ();  // open: out
  and and_1 (and_1_out, RST_N, D_IN[3]);
  and and_2 (and_2_out, RST_N, D_IN[2]);
  and and_3 (and_3_out, RST_N, D_IN[1]);
  and and_4 (and_4_out, RST_N, D_IN[0]);
  dff dff_1 (.CLK(in_2), .D(and_1_out), .Q(D_OUT[3]));  // open: nQ
  dff dff_2 (.CLK(in_2), .D(and_2_out), .Q(D_OUT[2]));  // open: nQ
  dff dff_3 (.CLK(in_2), .D(and_3_out), .Q(D_OUT[1]));  // open: nQ
  dff dff_4 (.CLK(in_2), .D(and_4_out), .Q(D_OUT[0]));  // open: nQ
endmodule

module _7 (
  input  in_1,
  output [3:0] out_2
);

  wire clock_1_out;
  wire [3:0] adder_1_out;

  Clock clock_1 (.out(clock_1_out));
  Adder #(.width(4)) adder_1 (.a(out_2), .b(4'b0001), .out(adder_1_out), .cin(1'b0));  // open: cout
  _6 u_6_1 (.D_IN(adder_1_out), .RST_N(in_1), .D_OUT(out_2), .in_2(clock_1_out));
endmodule

module EX1 (
  input  nS,
  input  nR,
  output Q,
  output nQ
);

  nand nand_1 (Q, nS, nQ);
  nand nand_2 (nQ, Q, nR);
endmodule

module EX2 (
  input  D,
  input  S,
  output Q,
  output nQ
);

  wire CLK_out, or_1_out;

  Clock CLK (.out(CLK_out));
  or or_1 (or_1_out, D, S);
  dff dff_1 (.CLK(CLK_out), .D(or_1_out), .Q(Q), .nQ(nQ));
endmodule

module ybz0 (
  input  R_n,
  input  D,
  input  CLK,
  output Q,
  output nQ
);

  wire and_1_out, CLK_out, dlatch_1_q, not_1_out, or_1_out;

  not not_1 (not_1_out, R_n);
  Clock u_CLK (.out(CLK_out));
  or or_1 (or_1_out, not_1_out, CLK_out);
  and and_1 (and_1_out, D, R_n);
  dlatch dlatch_1 (.CLK(or_1_out), .D(and_1_out), .Q(dlatch_1_q));  // open: out_4
  dlatch dlatch_2 (.CLK(or_1_out), .D(dlatch_1_q), .Q(Q), .out_4(nQ));

  // Notes on the sheet:
  //   时钟上升沿有效
endmodule

module reg1001 (
  input  [3:0] D_IN,
  input  CLK,
  input  RST,
  output [3:0] D_OUT
);

  wire and_1_out, and_2_out, not_1_out, not_2_out, or_1_out, or_2_out;

  Clock clock_1 ();  // open: out
  not not_1 (not_1_out, RST);
  not not_2 (not_2_out, RST);
  or or_1 (or_1_out, D_IN[3], not_1_out);
  and and_1 (and_1_out, D_IN[2], RST);
  and and_2 (and_2_out, D_IN[1], RST);
  or or_2 (or_2_out, D_IN[0], not_2_out);
  dff dff_1 (.CLK(CLK), .D(or_1_out), .Q(D_OUT[3]));  // open: nQ
  dff dff_2 (.CLK(CLK), .D(and_1_out), .Q(D_OUT[2]));  // open: nQ
  dff dff_3 (.CLK(CLK), .D(and_2_out), .Q(D_OUT[1]));  // open: nQ
  dff dff_4 (.CLK(CLK), .D(or_2_out), .Q(D_OUT[0]));  // open: nQ
endmodule

module EX4 (
  input  Set_9_n,
  output [3:0] out_2
);

  wire and_1_out, CLK_out, or_1_out;
  wire [3:0] subtractor_1_out;

  Clock CLK (.out(CLK_out));
  Subtractor #(.width(4)) subtractor_1 (.a(out_2), .b(4'b0001), .out(subtractor_1_out), .bin(1'b0));  // open: bout
  and and_1 (and_1_out, Set_9_n, or_1_out);
  or or_1 (or_1_out, out_2[0], out_2[1], out_2[2], out_2[3]);
  reg1001 reg1001_1 (.D_IN(subtractor_1_out), .CLK(CLK_out), .RST(and_1_out), .D_OUT(out_2));
endmodule
