// Logisim project week7-35.circ as structural Verilog: 14 circuits, main circuit SRLatch
module SRLatch (
  input  R,
  input  S,
  output Q,
  output nQ
);

  nor nor_1 (Q, R, nQ);
  nor nor_2 (nQ, Q, S);
endmodule

module DLatchr (
  input  reset,
  input  CLK,
  input  D,
  output Q,
  output nQ
);

  wire and_1_out, and_2_out, not_1_out, or_1_out;

  Clock clock_1 ();  // open: out
  not not_1 (not_1_out, D);
  and and_1 (and_1_out, CLK, not_1_out);
  and and_2 (and_2_out, CLK, D);
  or or_1 (or_1_out, reset, and_1_out);
  SRLatch srlatch_1 (.R(or_1_out), .S(and_2_out), .Q(Q), .nQ(nQ));
endmodule

module DFFR (
  input  CLK,
  input  D,
  output Q,
  output nQ
);

  wire dlatchr_1_q, not_1_out;

  Clock clock_1 ();  // open: out
  not not_1 (not_1_out, CLK);
  DLatchr dlatchr_1 (.CLK(not_1_out), .D(D), .Q(dlatchr_1_q));  // open: nQ, reset
  DLatchr dlatchr_2 (.CLK(CLK), .D(dlatchr_1_q), .Q(Q), .nQ(nQ));  // open: reset
endmodule

module TBZ0 (
  input  D,
  input  nRST,
  output Q,
  output nQ
);

  wire and_1_out, CLK_out;

  Clock CLK (.out(CLK_out));
  and and_1 (and_1_out, D, nRST);
  DFFR dffr_1 (.CLK(CLK_out), .D(and_1_out), .Q(Q), .nQ(nQ));
endmodule

module _6 (
  input  [3:0] D_IN,
  input  in_2,
  input  RST_N,
  output [3:0] D_OUT
);

  wire and_1_out, and_2_out, and_3_out, and_4_out;

  Clock CLK ();  // open: out
  and and_1 (and_1_out, RST_N, D_IN[3]);
  and and_2 (and_2_out, RST_N, D_IN[2]);
  and and_3 (and_3_out, RST_N, D_IN[1]);
  and and_4 (and_4_out, RST_N, D_IN[0]);
  DFFR dffr_1 (.CLK(in_2), .D(and_1_out), .Q(D_OUT[3]));  // open: nQ
  DFFR dffr_2 (.CLK(in_2), .D(and_2_out), .Q(D_OUT[2]));  // open: nQ
  DFFR dffr_3 (.CLK(in_2), .D(and_3_out), .Q(D_OUT[1]));  // open: nQ
  DFFR dffr_4 (.CLK(in_2), .D(and_4_out), .Q(D_OUT[0]));  // open: nQ
endmodule

module _7 (
  input  in_1,
  output [3:0] out_2
);

  wire clock_1_out;
  wire [3:0] adder_1_out;

  Clock clock_1 (.out(clock_1_out));
  Adder #(.width(4)) adder_1 (.a(out_2), .b(4'b0001), .out(adder_1_out), .cin(1'b0));  // open: cout
  _6 u_6_1 (.D_IN(adder_1_out), .RST_N(in_1), .D_OUT(out_2), .in_2(clock_1_out));
endmodule

module ex3_ybz0 (
  input  R_n,
  input  CLK,
  input  D,
  output Q,
  output nQ
);

  wire dlatchr_1_q, not_1_out, not_2_out;

  Clock u_CLK ();  // open: out
  not not_1 (not_1_out, R_n);
  not not_2 (not_2_out, CLK);
  DLatchr dlatchr_1 (.CLK(not_2_out), .D(D), .Q(dlatchr_1_q), .reset(not_1_out));  // open: nQ
  DLatchr dlatchr_2 (.CLK(CLK), .D(dlatchr_1_q), .Q(Q), .nQ(nQ), .reset(not_1_out));

  // Notes on the sheet:
  //   时钟上升沿有效
endmodule

module ex3_reg (
  input  [3:0] D_IN,
  input  CLK,
  input  RST,
  output [3:0] D_OUT
);

  Clock clock_1 ();  // open: out
  ex3_ybz0 ex3_ybz0_1 (.R_n(RST), .CLK(CLK), .D(D_IN[3]), .Q(D_OUT[3]));  // open: nQ
  ex3_ybz0 ex3_ybz0_2 (.R_n(RST), .CLK(CLK), .D(D_IN[2]), .Q(D_OUT[2]));  // open: nQ
  ex3_ybz0 ex3_ybz0_3 (.R_n(RST), .CLK(CLK), .D(D_IN[1]), .Q(D_OUT[1]));  // open: nQ
  ex3_ybz0 ex3_ybz0_4 (.R_n(RST), .CLK(CLK), .D(D_IN[0]), .Q(D_OUT[0]));  // open: nQ
endmodule

module ex3 (
  input  R_n,
  output [3:0] out_2
);

  wire CLK_out;
  wire [3:0] adder_1_out;

  Clock CLK (.out(CLK_out));
  Adder #(.width(4)) adder_1 (.a(out_2), .b(4'b0001), .out(adder_1_out), .cin(1'b0));  // open: cout
  ex3_reg ex3_reg_1 (.D_IN(adder_1_out), .D_OUT(out_2), .CLK(CLK_out), .RST(R_n));
endmodule

module ex4 (
  input  R_n,
  output [3:0] out_2
);

  wire and_1_out, and_2_out, CLK_out, not_1_out, not_2_out;
  wire [3:0] subtractor_1_out;

  Clock CLK (.out(CLK_out));
  Subtractor #(.width(4)) subtractor_1 (.a(out_2), .b(4'b0001), .out(subtractor_1_out));  // open: bin, bout
  and and_1 (and_1_out, R_n, and_2_out);
  and and_2 (and_2_out, out_2[0], not_1_out, not_2_out, out_2[3]);
  ex3_reg ex3_reg_1 (.D_IN(subtractor_1_out), .D_OUT(out_2), .CLK(CLK_out), .RST(and_1_out));
  not not_1 (not_1_out, out_2[1]);
  not not_2 (not_2_out, out_2[2]);
endmodule

module ex4_reg (
  input  [3:0] D_IN,
  input  CLK,
  input  RST,
  output [3:0] D_OUT
);

  wire clock_1_out;

  Clock clock_1 (.out(clock_1_out));
  ybz1 ybz1_1 (.S_n(clock_1_out), .CLK(RST), .D(D_IN[3]), .Q(D_OUT[3]));  // open: nQ
  ex3_ybz0 ex3_ybz0_1 (.R_n(RST), .CLK(clock_1_out), .D(D_IN[2]), .Q(D_OUT[2]));  // open: nQ
  ex3_ybz0 ex3_ybz0_2 (.R_n(RST), .CLK(clock_1_out), .D(D_IN[1]), .Q(D_OUT[1]));  // open: nQ
  ybz1 ybz1_2 (.S_n(clock_1_out), .CLK(RST), .D(D_IN[0]), .Q(D_OUT[0]));  // open: nQ
endmodule

module dlatchs (
  input  CLK,
  input  D,
  input  set,
  output Q,
  output nQ
);

  wire and_1_out, and_2_out, not_1_out, not_2_out, or_1_out;

  Clock clock_1 ();  // open: out
  not not_1 (not_1_out, D);
  not not_2 (not_2_out, set);
  and and_1 (and_1_out, CLK, D);
  and and_2 (and_2_out, CLK, not_2_out, not_1_out);
  or or_1 (or_1_out, and_1_out, set);
  SRLatch srlatch_1 (.R(and_2_out), .S(or_1_out), .Q(Q), .nQ(nQ));
endmodule

module ybz1 (
  input  S_n,
  input  CLK,
  input  D,
  output Q,
  output nQ
);

  wire dlatchs_1_q, not_1_out, not_2_out;

  not not_1 (not_1_out, S_n);
  Clock u_CLK ();  // open: out
  not not_2 (not_2_out, CLK);
  dlatchs dlatchs_1 (.CLK(not_2_out), .Q(dlatchs_1_q), .D(D), .set(not_1_out));  // open: nQ
  dlatchs dlatchs_2 (.CLK(CLK), .Q(Q), .nQ(nQ), .D(dlatchs_1_q), .set(not_1_out));
endmodule

module ex5 (
  input  R,
  output [3:0] out_2
);

  wire CLK_out, not_1_out;
  wire [3:0] adder_1_out;

  Clock CLK (.out(CLK_out));
  Adder #(.width(4)) adder_1 (.a(out_2), .b(4'b0001), .out(adder_1_out), .cin(1'b0));  // open: cout
  not not_1 (not_1_out, R);
  ex3_reg ex3_reg_1 (.D_IN(adder_1_out), .D_OUT(out_2), .CLK(CLK_out), .RST(not_1_out));
endmodule
